// Logisim project oficial.circ as structural Verilog: 4 circuits, main circuit main
module main (
  output [3:0] out_1,
  output [11:0] out_2,
  output [3:0] out_3,
  output [11:0] out_4,
  output [3:0] out_5,
  output [11:0] out_6,
  output [3:0] out_7,
  output [11:0] out_8,
  output [1:0] out_9,
  output [11:0] out_10,
  output [11:0] out_11
);

  wire and_1_out, and_2_out, BEQ, BPOS, BRANCH, CLK, JAL, JR, LW, MUX_ULA, or_1_out, POSITIVO, WRAM, WREG;
  wire [2:0] OPT_ULA;
  wire [3:0] multiplexer_3_out;
  wire [11:0] adder_1_out, bit_extender_2_out, multiplexer_1_out, multiplexer_2_out, multiplexer_4_out,
       multiplexer_7_out, PC_q, RB, ula_1_s;

  and and_1 (and_1_out, BEQ, BRANCH);
  and and_2 (and_2_out, BPOS, POSITIVO);
  Adder #(.width(12)) adder_1 (.a(PC_q), .b(multiplexer_4_out), .out(adder_1_out));  // open: cin, cout
  Multiplexer #(.width(12)) multiplexer_1 (.in0(out_2), .in1(adder_1_out), .out(multiplexer_1_out), .sel(or_1_out));
  or or_1 (or_1_out, and_1_out, JAL, and_2_out);
  Adder #(.width(12)) adder_2 (.a(PC_q), .b(12'h1), .out(out_2));  // open: cin, cout
  Clock clock_1 (.out(CLK));
  Multiplexer #(.width(12)) multiplexer_2 (.in0(multiplexer_1_out), .in1(out_4), .out(multiplexer_2_out), .sel(JR));
  Register #(.width(12)) PC (.D(multiplexer_2_out), .en(1'b1), .clk(CLK), .Q(PC_q));  // open: clr
  ROM #(.addrWidth(12), .dataWidth(12)) INSTRUCTIONS (.addr(PC_q), .data({out_5, out_1, out_3}));
  ROM #(.addrWidth(4), .dataWidth(13)) rom_1 (
    .addr(out_3), .data({JAL, WREG, MUX_ULA, OPT_ULA, WRAM, out_9, BRANCH, JR, BPOS, LW}));
  assign out_11 = {{4{out_5[3]}}, {out_5, out_1}};  // Bit_Extender bit_extender_1
  Multiplexer #(.width(4)) multiplexer_3 (.in0(out_1), .in1(4'b0000), .out(multiplexer_3_out), .sel(BRANCH));
  assign bit_extender_2_out = {{8{out_1[3]}}, out_1};  // Bit_Extender bit_extender_2
  Multiplexer #(.width(12)) multiplexer_4 (.in0(bit_extender_2_out), .in1(out_11), .out(multiplexer_4_out), .sel(JAL));
  register_bank register_bank_1 (
    .PCplus1(out_2), .JAL(JAL), .RA(out_5), .RB(multiplexer_3_out), .DATA(out_10), .WREG(WREG), .A(out_4),
    .B(RB));  // open: out_9
  Multiplexer #(.width(12)) multiplexer_5 (.in0(multiplexer_4_out), .in1(RB), .out(out_6), .sel(MUX_ULA));
  Multiplexer #(.select(2), .width(12)) multiplexer_6 (
    .in0(out_8), .in1(ula_1_s), .out(out_10), .sel(out_9));  // open: in2, in3
  nor nor_1 (POSITIVO, out_4[11], 1'b0);
  ULA ula_1 (.A(out_4), .B(out_6), .opcao(OPT_ULA), .S(ula_1_s));
  Multiplexer #(.width(12)) multiplexer_7 (.in0(out_4), .in1(RB), .out(multiplexer_7_out), .sel(LW));
  RAM #(.addrWidth(12), .dataWidth(12)) STACK (
    .addr(multiplexer_7_out), .we(WRAM), .oe(1'b1), .clk(CLK), .din(RB), .dout(out_8));
  Comparator #(.width(12)) comparator_1 (.a(ula_1_s), .b({12{1'b0}}), .eq(BEQ));  // open: gt, lt

  assign out_7 = out_1;

  // Other names for the same wires on the sheet: OPCODE[3:0] = out_3; DATA_REG[1:0] = out_9; IMM_JAL[11:0] = out_11;
  //   PCplus1[11:0] = out_2; RA[11:0] = out_4

  // Notes on the sheet:
  //   contents of INSTRUCTIONS (hex, n*v repeats v):
  //   20b 30b 47b 43b 541 541 541 641 772 721 262 268 779 222 271 21b f87 222 662 671 f61 61b 882 87b 83b
  //   442 47b 43b 21b 772 721 262 278 872 471 489 222 271 f07 772 222 721 332 442 4f1 41b 552 541 551 57b
  //   51b 772 222 271 21b 471 371 571 772 721 2f2 278 44a 33a a41 a31 5a9 f17
  //   contents of rom_1 (hex, n*v repeats v):
  //   780 c10 c90 d10 d90 e10 498 1790 792 7d0 c01 810 794
endmodule

module ULA (
  input  [11:0] A,
  input  [11:0] B,
  input  [2:0] opcao,
  output [11:0] S
);

  wire [11:0] adder_1_out, and_1_out, multiplier_1_out, not_1_out, or_1_out, subtractor_1_out;

  assign not_1_out = ~B;  // NOT_Gate not_1, 12 bits wide
  Adder #(.width(12)) adder_1 (.a(A), .b(B), .out(adder_1_out));  // open: cin, cout
  Subtractor #(.width(12)) subtractor_1 (.a(A), .b(B), .out(subtractor_1_out));  // open: bin, bout
  Multiplier #(.width(12)) multiplier_1 (.a(A), .b(B), .out(multiplier_1_out));  // open: cin, cout
  assign and_1_out = A & B;  // AND_Gate and_1, 12 bits wide
  assign or_1_out = A | B;  // OR_Gate or_1, 12 bits wide
  Multiplexer #(.select(3), .width(12)) multiplexer_1 (
    .in0(adder_1_out), .in1(subtractor_1_out), .in2(multiplier_1_out), .in3(and_1_out), .in4(or_1_out),
    .in5(not_1_out), .out(S), .sel(opcao));  // open: in6, in7
endmodule

module register_bank (
  input  [11:0] PCplus1,
  input  JAL,
  input  [3:0] RA,
  input  [3:0] RB,
  input  [11:0] DATA,
  input  WREG,
  output [11:0] A,
  output [11:0] B,
  output [3:0] out_9
);

  wire clock_1_out, W0, W1, W2, W3, W4, W5, W6, W7, W8, W9, W10, W11, W12, W13, W14, W15;
  wire [11:0] T1, T2, T3, T4, T5, T6, T7, T8, T9, T10, T11, T12, T13, T14, T15;

  Clock clock_1 (.out(clock_1_out));
  Demultiplexer #(.select(4)) demultiplexer_1 (
    .out0(W0), .out1(W1), .out2(W2), .out3(W3), .out4(W4), .out5(W5), .out6(W6), .out7(W7), .out8(W8),
    .out9(W9), .out10(W10), .out11(W11), .out12(W12), .out13(W13), .out14(W14), .out15(W15), .in(WREG),
    .sel(RA));
  Register #(.width(12)) R4 (.D(DATA), .en(W4), .clk(clock_1_out), .Q(T4));  // open: clr
  Register #(.width(12)) R8 (.D(DATA), .en(W8), .clk(clock_1_out), .Q(T8));  // open: clr
  Register #(.width(12)) R12 (.D(DATA), .en(W12), .clk(clock_1_out), .Q(T12));  // open: clr
  Register #(.width(12)) register_1 (.D(PCplus1), .en(JAL), .clk(clock_1_out), .Q(T1));  // open: clr
  Register #(.width(12)) R5 (.D(DATA), .en(W5), .clk(clock_1_out), .Q(T5));  // open: clr
  Register #(.width(12)) R9 (.D(DATA), .en(W9), .clk(clock_1_out), .Q(T9));  // open: clr
  Register #(.width(12)) R13 (.D(DATA), .en(W13), .clk(clock_1_out), .Q(T13));  // open: clr
  Register #(.width(12)) R2 (.D(DATA), .en(W2), .clk(clock_1_out), .Q(T2));  // open: clr
  Register #(.width(12)) R6 (.D(DATA), .en(W6), .clk(clock_1_out), .Q(T6));  // open: clr
  Register #(.width(12)) R10 (.D(DATA), .en(W10), .clk(clock_1_out), .Q(T10));  // open: clr
  Register #(.width(12)) R14 (.D(DATA), .en(W14), .clk(clock_1_out), .Q(T14));  // open: clr
  Register #(.width(12)) R3 (.D(DATA), .en(W3), .clk(clock_1_out), .Q(T3));  // open: clr
  Register #(.width(12)) R7 (.D(DATA), .en(W7), .clk(clock_1_out), .Q(T7));  // open: clr
  Register #(.width(12)) R11 (.D(DATA), .en(W11), .clk(clock_1_out), .Q(T11));  // open: clr
  Register #(.width(12)) R15 (.D(DATA), .en(W15), .clk(clock_1_out), .Q(T15));  // open: clr
  Multiplexer #(.select(4), .width(12)) multiplexer_1 (
    .in0({12{1'b0}}), .in1(T1), .in2(T2), .in3(T3), .in4(T4), .in5(T5), .in6(T6), .in7(T7), .in8(T8),
    .in9(T9), .in10(T10), .in11(T11), .in12(T12), .in13(T13), .in14(T14), .in15(T15), .out(A), .sel(RA));
  Multiplexer #(.select(4), .width(12)) multiplexer_2 (
    .in0({12{1'b0}}), .in1(T1), .in2(T2), .in3(T3), .in4(T4), .in5(T5), .in6(T6), .in7(T7), .in8(T8),
    .in9(T9), .in10(T10), .in11(T11), .in12(T12), .in13(T13), .in14(T14), .in15(T15), .out(B), .sel(RB));

  assign out_9 = RA;
endmodule

module UC (
  input  [3:0] OPCODE
);
endmodule
